# Fritzing sketch Midi_Out_ArduinoUno (saved by Fritzing 0.9.4)

parts:
  Part1 = Arduino Uno (Rev3)
  DIN1 = DIN-5 jack (MIDI) [package=THT]
  R2 = Resistor [tolerance=±5% resistance=220 package=THT]
  R1 = Resistor [tolerance=±5% resistance=220 package=THT]

nets:
  N1: Part1.D1/TX, R1.Pin_0
  N2: Part1.5V, R2.Pin_0
  N3: Part1.GND, DIN1.2
  N4: DIN1.5, R1.Pin_1
  N5: DIN1.4, R2.Pin_1

notes:
  2
  4
  5
  3
  1
  220 Ω
  TX / Digital pin 1
  5 pin DIN
  Arduino Uno 5V
  5V
  GND
