# Fritzing sketch Midi_out_Microbit (saved by Fritzing 0.9.4)

parts:
  Mod1 = Microbit
  DIN1 = DIN-5 jack (MIDI) [package=THT]
  R1 = Resistor [tolerance=±5% resistance=22 package=THT]
  R2 = Resistor [tolerance=±5% resistance=22 package=THT]

nets:
  N1: Mod1.P1, R2.Pin_0
  N2: Mod1.3V3, R1.Pin_0
  N3: Mod1.GND, DIN1.2
  N4: DIN1.5, R2.Pin_1
  N5: DIN1.4, R1.Pin_1

notes:
  22 Ω
  1
  3
  5
  4
  2
  Pin 1
  BBC Micro:bit 3.3V
  5 pin DIN
  3.3V
  GND

custom parts:
  Microbit: BBC Microbit Fritzing part. May 2019 expanded to include schematic and pcb views as well as breadboard. PCB view assumes an Adafruit PRODUCT ID: 3342 2x40 Right Angle through hole edge connector (although others will probably work as well). The pcb svg is custom (see forum article http://forum.fritzing.org/t/making-edge-connectors-and-both-side-smd-parts/7287 for an explaination if you need to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
